// Logisim project ex4.circ as structural Verilog: 5 circuits, main circuit RotRight
module RotRight (
  input  [15:0] INPUT0,
  input  [3:0] AMOUNT,
  output [15:0] OUTPUT0
);

  wire [15:0] rot1_2_out_2, rot2_2_out_2, x1, x2, x3, x4, x5, x6, x7, x8, x9, x10, x11, x12, x13, x14, x15;

  rot2 rot2_1 (.in_1(INPUT0), .out_2(x2));
  rot2 rot2_2 (.in_1(INPUT0), .out_2(rot2_2_out_2));
  rot1 rot1_1 (.in_1(INPUT0), .out_2(x1));
  rot4 rot4_1 (.in_1(rot2_2_out_2), .out_2(x6));
  rot2 rot2_3 (.in_1(x1), .out_2(x3));
  rot8 rot8_1 (.in_1(x6), .out_2(x14));
  rot4 rot4_2 (.in_1(x3), .out_2(x7));
  rot8 rot8_2 (.in_1(x7), .out_2(x15));
  rot4 rot4_3 (.in_1(INPUT0), .out_2(x4));
  Multiplexer #(.select(4), .width(16)) multiplexer_1 (
    .in0(INPUT0), .in1(x1), .in2(x2), .in3(x3), .in4(x4), .in5(x5), .in6(x6), .in7(x7), .in8(x8), .in9(x9),
    .in10(x10), .in11(x11), .in12(x12), .in13(x13), .in14(x14), .in15(x15), .out(OUTPUT0), .sel(AMOUNT));
  rot1 rot1_2 (.in_1(INPUT0), .out_2(rot1_2_out_2));
  rot8 rot8_3 (.in_1(x4), .out_2(x12));
  rot4 rot4_4 (.in_1(rot1_2_out_2), .out_2(x5));
  rot8 rot8_4 (.in_1(rot1_2_out_2), .out_2(x9));
  rot8 rot8_5 (.in_1(x5), .out_2(x13));
  rot2 rot2_4 (.in_1(x9), .out_2(x11));
  rot8 rot8_6 (.in_1(INPUT0), .out_2(x8));
  rot2 rot2_5 (.in_1(x8), .out_2(x10));

  // Other names for the same wires on the sheet: result[15:0] = OUTPUT0; X[3:0] = AMOUNT; x0[15:0] = INPUT0
endmodule

module rot1 (
  input  [15:0] in_1,
  output [15:0] out_2
);


  assign out_2 = {in_1[0], in_1[15:1]};
endmodule

module rot2 (
  input  [15:0] in_1,
  output [15:0] out_2
);


  assign out_2 = {in_1[1:0], in_1[15:2]};

  // Other names for the same wires on the sheet: B[13:0] = in_1[15:2]; A[1:0] = in_1[1:0]
endmodule

module rot4 (
  input  [15:0] in_1,
  output [15:0] out_2
);


  assign out_2 = {in_1[3:0], in_1[15:4]};

  // Other names for the same wires on the sheet: B[11:0] = in_1[15:4]; A[3:0] = in_1[3:0]
endmodule

module rot8 (
  input  [15:0] in_1,
  output [15:0] out_2
);


  assign out_2 = {in_1[7:0], in_1[15:8]};

  // Other names for the same wires on the sheet: B[7:0] = in_1[15:8]; A[7:0] = in_1[7:0]
endmodule
