// Logisim project partial-load.circ as structural Verilog: 1 circuit, main circuit partial_load
module partial_load (
  input  [31:0] Instruction,
  input  [31:0] MemAddress,
  input  [31:0] DataFromMem,
  output [31:0] DataToReg
);


  // Notes on the sheet:
  //   INPUTS to your circuit
  //   DON'T CHANGE THE LOCATIONS OF THE INPUTS AND OUTPUTS!
  //   OUTPUT from your circuit
endmodule
