// Logisim project branch-comp-unsigned.circ as structural Verilog: 1 circuit, main circuit main
module main (
  output [7:0] Test,
  output BrEq,
  output BrLt,
  output halt,
  output [31:0] BrData1,
  output [31:0] BrData2,
  output BrUn
);

  wire clock_1_out;
  wire [7:0] adder_1_out;

  Clock clock_1 (.out(clock_1_out));
  Adder adder_1 (.a(8'h1), .b(Test), .out(adder_1_out));  // open: cin, cout
  Register register_1 (.D(adder_1_out), .clk(clock_1_out), .Q(Test));  // open: en, clr
  ROM #(.dataWidth(32)) rom_1 (.addr(Test), .data(BrData1));
  Comparator comparator_1 (.a(Test), .b(8'h9), .eq(halt));  // open: gt, lt
  // Probe on BrUn
  // Probe on BrData1
  // Probe on BrData1
  ROM #(.dataWidth(32)) rom_2 (.addr(Test), .data(BrData2));
  branch_comp branch_comp_1 (.BrData1(BrData1), .BrData2(BrData1), .BrUn(BrUn), .BrEq(BrEq), .BrLt(BrLt));
  ROM #(.dataWidth(1)) rom_3 (.addr(Test), .data(BrUn));

  // Notes on the sheet:
  //   contents of rom_1 (hex, n*v repeats v):
  //   deadbeef 12345678 deadbeef 12345678 21524111 edcba988 abcdef12 12abcdef 161c162b
  //   Your branch_comp must fit here!
  //   contents of rom_2 (hex, n*v repeats v):
  //   deadbeef 12345678 21524111 edcba988 deadbeef 12345678 12abcdef abcdef12 161c162b
  //   There should be no red or blue wires, and the result should not be all X's
  //   contents of rom_3 (hex, n*v repeats v):
  //   1 1 1 1 1 1 1 1 1
endmodule
